// Logisim project LogiSim_Calc.circ as structural Verilog: 4 circuits, main circuit main
module main (
);

  wire _0, _1, _2, _3, _4, _5, _6, _7, _8, _9, adder_2_out_4, adder_3_out_4, adder_4_out_4, button_2_out,
       button_3_out, button_out, C, d_ff_1_q, d_ff_2_q, d_ff_2_qn, not_1_out, or_1_out, or_2_out, or_3_out,
       or_4_out, priority_encoder_1_gs, subtractor_1_out_14;
  wire [0:0] adder_1_out_4;
  wire [3:0] adder_1_out_5, adder_2_out_5, adder_3_out_5, adder_4_out_5, controlled_buffer_1_out,
       multiplexer_1_out, multiplexer_2_out, multiplexer_3_out, multiplexer_4_out, multiplexer_5_out,
       priority_encoder_1_out, shift_register_1_q0, shift_register_1_q1, shift_register_1_q2,
       shift_register_1_q3, shift_register_1_q4, shift_register_2_q0, shift_register_2_q1,
       shift_register_2_q2, shift_register_2_q3, subtractor_1_out_9, subtractor_1_out_10,
       subtractor_1_out_11, subtractor_1_out_12, subtractor_1_out_13;

  Button u__1 (.out(_1));
  Button u__4 (.out(_4));
  Button u__7 (.out(_7));
  Button u__2 (.out(_2));
  Button u__5 (.out(_5));
  Button u__8 (.out(_8));
  Button u__0 (.out(_0));
  Button u_C (.out(C));
  Priority_Encoder #(.select(4)) priority_encoder_1 (
    .in0(_0), .in1(_1), .in2(_2), .in3(_3), .in4(_4), .in5(_5), .in6(_6), .in7(_7), .in8(_8), .in9(_9),
    .out(priority_encoder_1_out), .gs(priority_encoder_1_gs));  // open: in10, in11, in12, in13, in14, in15, en_out, en_in
  Button u__3 (.out(_3));
  Button u__6 (.out(_6));
  Button u__9 (.out(_9));
  D_Flip_Flop d_ff_1 (.clk(button_3_out), .D(or_2_out), .Q(d_ff_1_q), .preset(C));  // open: Qn, en, reset
  or or_1 (or_1_out, C, or_4_out);
  or or_2 (or_2_out, subtractor_1_out_14, d_ff_2_qn);
  Hex_Digit_Display hex_digit_display_1 (.value(shift_register_1_q3));  // open: dp
  Hex_Digit_Display hex_digit_display_2 (.value(controlled_buffer_1_out));  // open: dp
  assign controlled_buffer_1_out = d_ff_1_q ? shift_register_1_q4 : 4'bz;  // Controlled_Buffer controlled_buffer_1
  not not_1 (not_1_out, button_3_out);
  or or_3 (or_3_out, priority_encoder_1_gs, button_3_out);
  Button button (.out(button_out));
  Button button_2 (.out(button_2_out));
  Button button_3 (.out(button_3_out));
  D_Flip_Flop d_ff_2 (
    .clk(button_2_out), .D(button_2_out), .Q(d_ff_2_q), .Qn(d_ff_2_qn), .reset(C));  // open: preset, en
  Hex_Digit_Display hex_digit_display_3 (.value(shift_register_1_q1));  // open: dp
  Hex_Digit_Display hex_digit_display_4 (.value(shift_register_1_q2));  // open: dp
  Shift_Register #(.width(4), .length(5)) shift_register_1 (
    .shift(not_1_out), .in(priority_encoder_1_out), .clk(or_3_out), .load(button_3_out), .clr(or_1_out),
    .d0(multiplexer_5_out), .q0(shift_register_1_q0), .d1(multiplexer_4_out), .q1(shift_register_1_q1),
    .d2(multiplexer_3_out), .q2(shift_register_1_q2), .d3(multiplexer_2_out), .q3(shift_register_1_q3),
    .d4(multiplexer_1_out), .q4(shift_register_1_q4));  // open: out
  Shift_Register #(.width(4), .length(4)) shift_register_2 (
    .shift(1'b0), .clk(or_4_out), .load(or_4_out), .d0(shift_register_1_q0), .q0(shift_register_2_q0),
    .d1(shift_register_1_q1), .q1(shift_register_2_q1), .d2(shift_register_1_q2), .q2(shift_register_2_q2),
    .d3(shift_register_1_q3), .q3(shift_register_2_q3));  // open: in, out, clr
  Hex_Digit_Display hex_digit_display_5 (.value(shift_register_1_q0));  // open: dp
  or or_4 (or_4_out, button_out, button_2_out);
  adder adder_1 (
    .in_2(shift_register_2_q3), .in_3(shift_register_1_q3), .in_1(adder_2_out_4), .out_4(adder_1_out_4[0]),
    .out_5(adder_1_out_5));
  Multiplexer #(.width(4)) multiplexer_1 (
    .in0({3'b000, adder_1_out_4[0]}), .in1(subtractor_1_out_13), .out(multiplexer_1_out), .sel(d_ff_2_q));  // open: en
  adder adder_2 (
    .in_2(shift_register_2_q2), .in_3(shift_register_1_q2), .in_1(adder_3_out_4), .out_4(adder_2_out_4),
    .out_5(adder_2_out_5));
  Multiplexer #(.width(4)) multiplexer_2 (
    .in0(adder_1_out_5), .in1(subtractor_1_out_12), .out(multiplexer_2_out), .sel(d_ff_2_q));  // open: en
  adder adder_3 (
    .in_2(shift_register_2_q1), .in_3(shift_register_1_q1), .in_1(adder_4_out_4), .out_4(adder_3_out_4),
    .out_5(adder_3_out_5));
  Multiplexer #(.width(4)) multiplexer_3 (
    .in0(adder_2_out_5), .in1(subtractor_1_out_11), .out(multiplexer_3_out), .sel(d_ff_2_q));  // open: en
  adder adder_4 (
    .in_2(shift_register_2_q0), .in_3(shift_register_1_q0), .in_1(1'b0), .out_4(adder_4_out_4),
    .out_5(adder_4_out_5));
  Multiplexer #(.width(4)) multiplexer_4 (
    .in0(adder_3_out_5), .in1(subtractor_1_out_10), .out(multiplexer_4_out), .sel(d_ff_2_q));  // open: en
  Multiplexer #(.width(4)) multiplexer_5 (
    .in0(adder_4_out_5), .in1(subtractor_1_out_9), .out(multiplexer_5_out), .sel(d_ff_2_q));  // open: en
  subtractor subtractor_1 (
    .in_1(shift_register_2_q0), .in_2(shift_register_1_q0), .in_3(shift_register_2_q1),
    .in_4(shift_register_1_q1), .in_5(shift_register_2_q2), .in_6(shift_register_1_q2),
    .in_7(shift_register_2_q3), .in_8(shift_register_1_q3), .out_13(subtractor_1_out_13),
    .out_9(subtractor_1_out_9), .out_10(subtractor_1_out_10), .out_11(subtractor_1_out_11),
    .out_12(subtractor_1_out_12), .out_14(subtractor_1_out_14));
endmodule

module adder (
  input  in_1,
  input  [3:0] in_2,
  input  [3:0] in_3,
  output out_4,
  output [3:0] out_5
);

  wire adder_1_cout, and_1_out, and_2_out;
  wire [3:0] adder_1_out;

  Adder #(.width(4)) adder_1 (.a(in_2), .b(in_3), .out(adder_1_out), .cin(in_1), .cout(adder_1_cout));
  or or_1 (out_4, adder_1_cout, and_1_out, and_2_out);
  and and_1 (and_1_out, adder_1_out[3], adder_1_out[2]);
  and and_2 (and_2_out, adder_1_out[3], adder_1_out[1]);
  Adder #(.width(4)) adder_2 (.a(adder_1_out), .b({1'b0, {2{out_4}}, 1'b0}), .out(out_5));  // open: cin, cout
endmodule

module subtractor (
  input  [3:0] in_1,
  input  [3:0] in_2,
  input  [3:0] in_3,
  input  [3:0] in_4,
  input  [3:0] in_5,
  input  [3:0] in_6,
  input  [3:0] in_7,
  input  [3:0] in_8,
  output [3:0] out_9,
  output [3:0] out_10,
  output [3:0] out_11,
  output [3:0] out_12,
  output [3:0] out_13,
  output out_14
);

  wire adder_1_out_4, adder_2_out_4, adder_3_out_4, adder_5_out_4, adder_6_out_4, adder_7_out_4;
  wire [3:0] adder_1_out_5, adder_2_out_5, adder_3_out_5, adder_4_out_5, adder_5_out_5, adder_6_out_5,
       adder_7_out_5, adder_8_out_5, complement_1_out_2, complement_2_out_2, complement_3_out_2,
       complement_4_out_2, complement_5_out_2, complement_6_out_2, complement_7_out_2, complement_8_out_2;

  complement complement_1 (.in_1(in_2), .out_2(complement_1_out_2));
  complement complement_2 (.in_1(in_4), .out_2(complement_2_out_2));
  complement complement_3 (.in_1(in_6), .out_2(complement_3_out_2));
  complement complement_4 (.in_1(in_8), .out_2(complement_4_out_2));
  adder adder_1 (.in_2(complement_1_out_2), .in_3(in_1), .in_1(1'b1), .out_4(adder_1_out_4), .out_5(adder_1_out_5));
  adder adder_2 (
    .in_2(complement_2_out_2), .in_3(in_3), .in_1(adder_1_out_4), .out_4(adder_2_out_4), .out_5(adder_2_out_5));
  adder adder_3 (
    .in_2(complement_3_out_2), .in_3(in_5), .in_1(adder_2_out_4), .out_4(adder_3_out_4), .out_5(adder_3_out_5));
  adder adder_4 (.in_2(complement_4_out_2), .in_3(in_7), .in_1(adder_3_out_4), .out_4(out_14), .out_5(adder_4_out_5));
  complement complement_5 (.in_1(adder_1_out_5), .out_2(complement_5_out_2));
  complement complement_6 (.in_1(adder_2_out_5), .out_2(complement_6_out_2));
  complement complement_7 (.in_1(adder_3_out_5), .out_2(complement_7_out_2));
  complement complement_8 (.in_1(adder_4_out_5), .out_2(complement_8_out_2));
  adder adder_5 (.in_2(4'b0000), .in_3(complement_5_out_2), .in_1(1'b1), .out_4(adder_5_out_4), .out_5(adder_5_out_5));
  Multiplexer #(.width(4)) multiplexer_1 (
    .in0(adder_5_out_5), .in1(adder_1_out_5), .out(out_9), .sel(out_14));  // open: en
  adder adder_6 (
    .in_2(4'b0000), .in_3(complement_6_out_2), .in_1(adder_5_out_4), .out_4(adder_6_out_4),
    .out_5(adder_6_out_5));
  Multiplexer #(.width(4)) multiplexer_2 (
    .in0(adder_6_out_5), .in1(adder_2_out_5), .out(out_10), .sel(out_14));  // open: en
  adder adder_7 (
    .in_2(4'b0000), .in_3(complement_7_out_2), .in_1(adder_6_out_4), .out_4(adder_7_out_4),
    .out_5(adder_7_out_5));
  Multiplexer #(.width(4)) multiplexer_3 (
    .in0(adder_7_out_5), .in1(adder_3_out_5), .out(out_11), .sel(out_14));  // open: en
  adder adder_8 (
    .in_2(4'b0000), .in_3(complement_8_out_2), .in_1(adder_7_out_4), .out_5(adder_8_out_5));  // open: out_4
  Multiplexer #(.width(4)) multiplexer_4 (
    .in0(adder_8_out_5), .in1(adder_4_out_5), .out(out_12), .sel(out_14));  // open: en

  assign out_13 = 4'b0000;
endmodule

module complement (
  input  [3:0] in_1,
  output [3:0] out_2
);

  wire and_1_out, and_2_out, and_4_out, not_1_out, not_2_out, not_3_out;

  not not_1 (not_1_out, in_1[3]);
  not not_2 (not_2_out, in_1[2]);
  and and_1 (and_1_out, not_1_out, not_2_out);
  not not_3 (not_3_out, in_1[1]);
  and and_2 (and_2_out, not_1_out, not_2_out, in_1[1]);
  and and_3 (out_2[3], and_1_out, not_3_out);
  or or_1 (out_2[2], and_2_out, and_4_out);
  not not_4 (out_2[0], in_1[0]);
  and and_4 (and_4_out, not_1_out, in_1[2], not_3_out);
  and and_5 (out_2[1], not_1_out, in_1[1]);
endmodule
